# Fritzing sketch Schematics (saved by Fritzing 0.9.3b)
circuit board: 11.7382cm x 5.79095cm
breadboards: 1

parts:
  Arduino_Uno = Arduino Uno (Rev3)
  G = NPN-Transistor [package="TO92 [THT]"]
  S1 = Momentary Switch [package=ksa_sealed_tac_switch]
  U1 = POT [package=trim_pot]
  R = NPN-Transistor [package="TO92 [THT]"]
  B = NPN-Transistor [package="TO92 [THT]"]
  R1 = Resistor [tolerance=±5% resistance=200 package=THT]
  LED_Strip = double row male pin header, 4 pins [form="♂ (male)"]

nets:
  N1: Arduino_Uno.A0, U1.E
  N2: Arduino_Uno.D2, S1.3, R1.Pin_1
  N3: Arduino_Uno.D3_PWM, G.B
  N4: Arduino_Uno.D5_PWM, R.B
  N5: Arduino_Uno.D6_PWM, B.B
  N6: Arduino_Uno.5V, S1.1, U1.S, LED_Strip.pin1
  N7: Arduino_Uno.GND, G.C, U1.A, R.C, B.C, R1.Pin_0
  N8: G.E, LED_Strip.pin2
  N9: R.E, LED_Strip.pin3
  N10: B.E, LED_Strip.pin4
